# Fritzing sketch matrix_keypad (saved by Fritzing 0.7.12b)
breadboards: 1

parts:
  pyMCU_v1_1 = pyMCU
  KEYPAD1 = Membrane Matrix Keypad
  R1 = Resistor [tolerance=±5% resistance=10k package=THT]
  R2 = Resistor [tolerance=±5% resistance=10k package=THT]
  R3 = Resistor [tolerance=±5% resistance=10k package=THT]
  R4 = Resistor [tolerance=±5% resistance=10k package=THT]
  R5 = Resistor [tolerance=±5% resistance=10k package=THT]
  R6 = Resistor [tolerance=±5% resistance=10k package=THT]
  R7 = Resistor [tolerance=±5% resistance=10k package=THT]

nets:
  N1: pyMCU_v1_1.D1, KEYPAD1.7, R7.Pin_0
  N2: pyMCU_v1_1.D2, KEYPAD1.6, R6.Pin_0
  N3: pyMCU_v1_1.D3, KEYPAD1.5, R5.Pin_0
  N4: pyMCU_v1_1.D4, KEYPAD1.4, R4.Pin_0
  N5: pyMCU_v1_1.D5, KEYPAD1.3, R3.Pin_0
  N6: pyMCU_v1_1.D6, KEYPAD1.2, R2.Pin_0
  N7: pyMCU_v1_1.D7, KEYPAD1.1, R1.Pin_0
  N8: pyMCU_v1_1.GND, R5.Pin_1, R6.Pin_1, R7.Pin_1
  N9: pyMCU_v1_1.VCC, R1.Pin_1, R2.Pin_1, R3.Pin_1, R4.Pin_1

custom parts:
  pyMCU: pyMCU - Python Controlled Microcontroller http://www.pymcu.com
  Membrane Matrix Keypad: Membrane Matrix 3x4 Keypad
